// Logisim project mips_cpu_g1.circ as structural Verilog: 9 circuits, main circuit main
module main (
  input  in_1
);

  wire alu_1_zero, ALUSrc, and_1_out, Branch, CLK, control_1_regwrite, Jump, JumpLink, jumpregister, MemRead,
       MemToReg, MemWrite, RegDst, SingleByte;
  wire [1:0] control_1_aluop;
  wire [2:0] alucontrol_1_aluctrl;
  wire [4:0] ibreakdown_1_rd, ibreakdown_1_rs, ibreakdown_1_rt, multiplexer_1_out, multiplexer_2_out, shamt;
  wire [5:0] ibreakdown_1_funct, ibreakdown_1_op;
  wire [7:0] memorydata_1_memorybyte;
  wire [15:0] ibreakdown_1_fmm;
  wire [25:0] ibreakdown_1_address;
  wire [27:0] ifetch_1_pcplus4;
  wire [31:0] adder_1_out, alu_1_result, bit_extender_1_out, ByteConSigno, ifetch_1_instruction,
       memorydata_1_readdata, multiplexer_3_out, multiplexer_4_out, multiplexer_5_out, multiplexer_6_out,
       multiplexer_7_out, multiplexer_8_out, ReadData2, rf_1_readdata1, shifter_2_out, WriteData;
  wire [31:2] JumpAddress;

  Clock clock_1 (.out(CLK));
  // Probe on {JumpAddress[31:28], ifetch_1_pcplus4}
  // Probe on ifetch_1_instruction
  IFetch ifetch_1 (
    .PCnext(multiplexer_7_out), .CLK(CLK), .Reset(in_1), .PCplus4({JumpAddress[31:28], ifetch_1_pcplus4}),
    .instruction(ifetch_1_instruction));
  IBreakdown ibreakdown_1 (
    .Instruction(ifetch_1_instruction), .Op(ibreakdown_1_op), .address(ibreakdown_1_address),
    .rs(ibreakdown_1_rs), .rt(ibreakdown_1_rt), .rd(ibreakdown_1_rd), .shamt(shamt), .fmm(ibreakdown_1_fmm),
    .funct(ibreakdown_1_funct));
  Shifter #(.width(26)) shifter_1 (.in(ibreakdown_1_address), .\dist (5'b00010), .out(JumpAddress[27:2]));
  // Probe on ibreakdown_1_rs
  Multiplexer #(.width(5)) multiplexer_1 (
    .in0(ibreakdown_1_rt), .in1(ibreakdown_1_rd), .out(multiplexer_1_out), .sel(RegDst));
  // Probe on ibreakdown_1_fmm
  Multiplexer #(.width(5)) multiplexer_2 (
    .in0(multiplexer_1_out), .in1({5{1'b1}}), .out(multiplexer_2_out), .sel(JumpLink));
  assign bit_extender_1_out = {{16{ibreakdown_1_fmm[15]}}, ibreakdown_1_fmm};  // Bit_Extender bit_extender_1
  // Probe on multiplexer_2_out
  Multiplexer #(.width(32)) multiplexer_3 (
    .in0(WriteData), .in1({JumpAddress, 2'b00}), .out(multiplexer_3_out), .sel(JumpLink));
  Control control_1 (
    .opcode(ibreakdown_1_op), .RegDst(RegDst), .Jump(Jump), .Branch(Branch), .MemRead(MemRead),
    .MemtoReg(MemToReg), .ALUOp(control_1_aluop), .MemWrite(MemWrite), .ALUSrc(ALUSrc),
    .RegWrite(control_1_regwrite), .SyngleByte(SingleByte), .JumpLink(JumpLink));
  // Probe on shifter_2_out
  // Probe on multiplexer_2_out
  Shifter #(.width(32)) shifter_2 (.in(bit_extender_1_out), .\dist (5'b00010), .out(shifter_2_out));
  // Probe on multiplexer_3_out
  // Probe on control_1_aluop
  // Probe on ibreakdown_1_funct
  // Probe on alucontrol_1_aluctrl
  Adder #(.width(32)) adder_1 (
    .a({JumpAddress[31:28], ifetch_1_pcplus4}), .b(shifter_2_out), .out(adder_1_out));  // open: cin, cout
  RF rf_1 (
    .ReadReg1(ibreakdown_1_rs), .ReadReg2(ibreakdown_1_rt), .WriteReg(multiplexer_2_out),
    .RegWrite(control_1_regwrite), .WriteData(multiplexer_3_out), .CLK(CLK), .Reset(in_1),
    .ReadData1(rf_1_readdata1), .ReadData2(ReadData2));
  ALUControl alucontrol_1 (
    .ALUOp(control_1_aluop), .funct(ibreakdown_1_funct), .ALUCtrl(alucontrol_1_aluctrl),
    .jumpregister(jumpregister));
  // Probe on rf_1_readdata1
  // Probe on adder_1_out
  Multiplexer #(.width(32)) multiplexer_4 (
    .in0(ReadData2), .in1(bit_extender_1_out), .out(multiplexer_4_out), .sel(ALUSrc));
  ALU alu_1 (
    .Input1(rf_1_readdata1), .Input2(multiplexer_4_out), .ALUOperation(alucontrol_1_aluctrl), .shamt(shamt),
    .Zero(alu_1_zero), .Result(alu_1_result));
  and and_1 (and_1_out, Branch, alu_1_zero);
  // Probe on alu_1_result
  Multiplexer #(.width(32)) multiplexer_5 (
    .in0({JumpAddress[31:28], ifetch_1_pcplus4}), .in1(adder_1_out), .out(multiplexer_5_out), .sel(and_1_out));
  Multiplexer #(.width(32)) multiplexer_6 (
    .in0(multiplexer_5_out), .in1({JumpAddress, 2'b00}), .out(multiplexer_6_out), .sel(Jump));
  MemoryData memorydata_1 (
    .address(alu_1_result), .WriteData(ReadData2), .MemWrite(MemWrite), .MemRead(MemRead), .CLK(CLK),
    .Reset(in_1), .ReadData(memorydata_1_readdata), .MemoryByte(memorydata_1_memorybyte));
  Multiplexer #(.width(32)) multiplexer_7 (
    .in0(multiplexer_6_out), .in1(WriteData), .out(multiplexer_7_out), .sel(jumpregister));
  // Probe on memorydata_1_readdata
  assign ByteConSigno = {{24{memorydata_1_memorybyte[7]}}, memorydata_1_memorybyte};  // Bit_Extender bit_extender_2
  Multiplexer #(.width(32)) multiplexer_8 (
    .in0(memorydata_1_readdata), .in1(ByteConSigno), .out(multiplexer_8_out), .sel(SingleByte));
  // Probe on multiplexer_7_out
  // Probe on multiplexer_8_out
  // Probe on WriteData
  Multiplexer #(.width(32)) multiplexer_9 (
    .in0(alu_1_result), .in1(multiplexer_8_out), .out(WriteData), .sel(MemToReg));

  // Other names for the same wires on the sheet: Upper4PC4[3:0] = JumpAddress[31:28]; Reset = in_1
endmodule

module RF (
  input  [4:0] ReadReg1,
  input  [4:0] ReadReg2,
  input  [4:0] WriteReg,
  input  RegWrite,
  input  [31:0] WriteData,
  input  CLK,
  input  Reset,
  output [31:0] ReadData1,
  output [31:0] ReadData2
);

  wire [6:0] decoder_1_out1;
  wire [7:0] decoder_1_out8, decoder_1_out16, decoder_1_out24;
  wire [31:0] ReadR0, ReadR1, ReadR2, ReadR3, ReadR4, ReadR5, ReadR6, ReadR7, ReadR8, ReadR9, ReadR10,
       ReadR11, ReadR12, ReadR13, ReadR14, ReadR15, ReadR16, ReadR17, ReadR18, ReadR19, ReadR20, ReadR21,
       ReadR22, ReadR23, ReadR24, ReadR25, ReadR26, ReadR27, ReadR28, ReadR29, ReadR30, ReadR31;

  Decoder #(.select(5)) decoder_1 (
    .out1(decoder_1_out1[0]), .out2(decoder_1_out1[1]), .out3(decoder_1_out1[2]), .out4(decoder_1_out1[3]),
    .out5(decoder_1_out1[4]), .out6(decoder_1_out1[5]), .out7(decoder_1_out1[6]), .out8(decoder_1_out8[0]),
    .out9(decoder_1_out8[1]), .out10(decoder_1_out8[2]), .out11(decoder_1_out8[3]),
    .out12(decoder_1_out8[4]), .out13(decoder_1_out8[5]), .out14(decoder_1_out8[6]),
    .out15(decoder_1_out8[7]), .out16(decoder_1_out16[0]), .out17(decoder_1_out16[1]),
    .out18(decoder_1_out16[2]), .out19(decoder_1_out16[3]), .out20(decoder_1_out16[4]),
    .out21(decoder_1_out16[5]), .out22(decoder_1_out16[6]), .out23(decoder_1_out16[7]),
    .out24(decoder_1_out24[0]), .out25(decoder_1_out24[1]), .out26(decoder_1_out24[2]),
    .out27(decoder_1_out24[3]), .out28(decoder_1_out24[4]), .out29(decoder_1_out24[5]),
    .out30(decoder_1_out24[6]), .out31(decoder_1_out24[7]), .sel(WriteReg), .en(RegWrite));  // open: out0
  Register #(.width(32)) R0 (.D(WriteData), .en(1'b0), .clk(CLK), .Q(ReadR0), .clr(Reset));
  Register #(.width(32)) R1 (.D(WriteData), .en(decoder_1_out1[0]), .clk(CLK), .Q(ReadR1), .clr(Reset));
  Register #(.width(32)) R2 (.D(WriteData), .en(decoder_1_out1[1]), .clk(CLK), .Q(ReadR2), .clr(Reset));
  Register #(.width(32)) R3 (.D(WriteData), .en(decoder_1_out1[2]), .clk(CLK), .Q(ReadR3), .clr(Reset));
  Register #(.width(32)) R4 (.D(WriteData), .en(decoder_1_out1[3]), .clk(CLK), .Q(ReadR4), .clr(Reset));
  Register #(.width(32)) R5 (.D(WriteData), .en(decoder_1_out1[4]), .clk(CLK), .Q(ReadR5), .clr(Reset));
  Register #(.width(32)) R6 (.D(WriteData), .en(decoder_1_out1[5]), .clk(CLK), .Q(ReadR6), .clr(Reset));
  Register #(.width(32)) R7 (.D(WriteData), .en(decoder_1_out1[6]), .clk(CLK), .Q(ReadR7), .clr(Reset));
  Multiplexer #(.select(5), .width(32)) multiplexer_1 (
    .in0(ReadR0), .in1(ReadR1), .in2(ReadR2), .in3(ReadR3), .in4(ReadR4), .in5(ReadR5), .in6(ReadR6),
    .in7(ReadR7), .in8(ReadR8), .in9(ReadR9), .in10(ReadR10), .in11(ReadR11), .in12(ReadR12), .in13(ReadR13),
    .in14(ReadR14), .in15(ReadR15), .in16(ReadR16), .in17(ReadR17), .in18(ReadR18), .in19(ReadR19),
    .in20(ReadR20), .in21(ReadR21), .in22(ReadR22), .in23(ReadR23), .in24(ReadR24), .in25(ReadR25),
    .in26(ReadR26), .in27(ReadR27), .in28(ReadR28), .in29(ReadR29), .in30(ReadR30), .in31(ReadR31),
    .out(ReadData1), .sel(ReadReg1));
  Register #(.width(32)) R8 (.D(WriteData), .en(decoder_1_out8[0]), .clk(CLK), .Q(ReadR8), .clr(Reset));
  Register #(.width(32)) R9 (.D(WriteData), .en(decoder_1_out8[1]), .clk(CLK), .Q(ReadR9), .clr(Reset));
  Register #(.width(32)) R10 (.D(WriteData), .en(decoder_1_out8[2]), .clk(CLK), .Q(ReadR10), .clr(Reset));
  Register #(.width(32)) R11 (.D(WriteData), .en(decoder_1_out8[3]), .clk(CLK), .Q(ReadR11), .clr(Reset));
  Register #(.width(32)) R12 (.D(WriteData), .en(decoder_1_out8[4]), .clk(CLK), .Q(ReadR12), .clr(Reset));
  Register #(.width(32)) R13 (.D(WriteData), .en(decoder_1_out8[5]), .clk(CLK), .Q(ReadR13), .clr(Reset));
  Register #(.width(32)) R14 (.D(WriteData), .en(decoder_1_out8[6]), .clk(CLK), .Q(ReadR14), .clr(Reset));
  Register #(.width(32)) R15 (.D(WriteData), .en(decoder_1_out8[7]), .clk(CLK), .Q(ReadR15), .clr(Reset));
  Register #(.width(32)) R16 (.D(WriteData), .en(decoder_1_out16[0]), .clk(CLK), .Q(ReadR16), .clr(Reset));
  Register #(.width(32)) R17 (.D(WriteData), .en(decoder_1_out16[1]), .clk(CLK), .Q(ReadR17), .clr(Reset));
  Register #(.width(32)) R18 (.D(WriteData), .en(decoder_1_out16[2]), .clk(CLK), .Q(ReadR18), .clr(Reset));
  Register #(.width(32)) R19 (.D(WriteData), .en(decoder_1_out16[3]), .clk(CLK), .Q(ReadR19), .clr(Reset));
  Register #(.width(32)) R20 (.D(WriteData), .en(decoder_1_out16[4]), .clk(CLK), .Q(ReadR20), .clr(Reset));
  Register #(.width(32)) R21 (.D(WriteData), .en(decoder_1_out16[5]), .clk(CLK), .Q(ReadR21), .clr(Reset));
  Register #(.width(32)) R22 (.D(WriteData), .en(decoder_1_out16[6]), .clk(CLK), .Q(ReadR22), .clr(Reset));
  Register #(.width(32)) R23 (.D(WriteData), .en(decoder_1_out16[7]), .clk(CLK), .Q(ReadR23), .clr(Reset));
  Register #(.width(32)) R24 (.D(WriteData), .en(decoder_1_out24[0]), .clk(CLK), .Q(ReadR24), .clr(Reset));
  Register #(.width(32)) R25 (.D(WriteData), .en(decoder_1_out24[1]), .clk(CLK), .Q(ReadR25), .clr(Reset));
  Register #(.width(32)) R26 (.D(WriteData), .en(decoder_1_out24[2]), .clk(CLK), .Q(ReadR26), .clr(Reset));
  Register #(.width(32)) R27 (.D(WriteData), .en(decoder_1_out24[3]), .clk(CLK), .Q(ReadR27), .clr(Reset));
  Register #(.width(32)) R28 (.D(WriteData), .en(decoder_1_out24[4]), .clk(CLK), .Q(ReadR28), .clr(Reset));
  Register #(.width(32)) R29 (.D(WriteData), .en(decoder_1_out24[5]), .clk(CLK), .Q(ReadR29), .clr(Reset));
  Register #(.width(32)) R30 (.D(WriteData), .en(decoder_1_out24[6]), .clk(CLK), .Q(ReadR30), .clr(Reset));
  Register #(.width(32)) R31 (.D(WriteData), .en(decoder_1_out24[7]), .clk(CLK), .Q(ReadR31), .clr(Reset));
  Multiplexer #(.select(5), .width(32)) multiplexer_2 (
    .in0(ReadR0), .in1(ReadR1), .in2(ReadR2), .in3(ReadR3), .in4(ReadR4), .in5(ReadR5), .in6(ReadR6),
    .in7(ReadR7), .in8(ReadR8), .in9(ReadR9), .in10(ReadR10), .in11(ReadR11), .in12(ReadR12), .in13(ReadR13),
    .in14(ReadR14), .in15(ReadR15), .in16(ReadR16), .in17(ReadR17), .in18(ReadR18), .in19(ReadR19),
    .in20(ReadR20), .in21(ReadR21), .in22(ReadR22), .in23(ReadR23), .in24(ReadR24), .in25(ReadR25),
    .in26(ReadR26), .in27(ReadR27), .in28(ReadR28), .in29(ReadR29), .in30(ReadR30), .in31(ReadR31),
    .out(ReadData2), .sel(ReadReg2));
endmodule

module ALU (
  input  [31:0] Input1,
  input  [31:0] Input2,
  input  [2:0] ALUOperation,
  input  [4:0] shamt,
  output Zero,
  output [31:0] Result
);

  wire comparator_1_lt;
  wire [31:0] adder_1_out, and_1_out, bit_extender_1_out, not_1_out, or_1_out, shifter_1_out,
       subtractor_1_out;

  Adder #(.width(32)) adder_1 (.a(Input1), .b(Input2), .out(adder_1_out));  // open: cin, cout
  assign or_1_out = Input1 | Input2;  // OR_Gate or_1, 32 bits wide
  Comparator #(.width(32)) comparator_1 (.a(Input1), .b(Input2), .lt(comparator_1_lt));  // open: gt, eq
  Subtractor #(.width(32)) subtractor_1 (.a(Input1), .b(Input2), .out(subtractor_1_out));  // open: bin, bout
  assign and_1_out = Input1 & Input2;  // AND_Gate and_1, 32 bits wide
  Shifter #(.shift("lr"), .width(32)) shifter_1 (.in(Input2), .\dist (shamt), .out(shifter_1_out));
  assign bit_extender_1_out = {{31{1'b0}}, comparator_1_lt};  // Bit_Extender bit_extender_1
  assign not_1_out = ~or_1_out;  // NOT_Gate not_1, 32 bits wide
  Multiplexer #(.select(3), .width(32)) multiplexer_1 (
    .in0(adder_1_out), .in1(or_1_out), .in2(bit_extender_1_out), .in3(not_1_out), .in4(subtractor_1_out),
    .in5(and_1_out), .in6(shifter_1_out), .out(Result), .sel(ALUOperation));  // open: in7
  Comparator #(.width(32)) comparator_2 (.a(Result), .b({32{1'b0}}), .eq(Zero));  // open: gt, lt
endmodule

module IFetch (
  input  [31:0] PCnext,
  input  CLK,
  input  Reset,
  output [31:0] PCplus4,
  output [31:0] instruction
);

  wire [31:0] PCreg_q;

  Register #(.width(32)) PCreg (.D(PCnext), .clk(CLK), .Q(PCreg_q), .clr(Reset));  // open: en
  // Probe on PCreg_q
  Adder #(.width(32)) adder_1 (.a(PCreg_q), .b(32'h4), .out(PCplus4));  // open: cin, cout
  // Probe on PCreg_q[25:2]
  ROM #(.addrWidth(24), .dataWidth(32)) rom_1 (.addr(PCreg_q[25:2]), .data(instruction));

  // Notes on the sheet:
  //   contents of rom_1 (hex, n*v repeats v):
  //   8c080000 8c090004 1095025 1095824 1096020 1096822 ac0d000c 1095027 128582a
endmodule

module IBreakdown (
  input  [31:0] Instruction,
  output [5:0] Op,
  output [25:0] address,
  output [4:0] rs,
  output [4:0] rt,
  output [4:0] rd,
  output [4:0] shamt,
  output [15:0] fmm,
  output [5:0] funct
);


  assign address = Instruction[25:0];
  assign fmm = Instruction[15:0];
  assign funct = Instruction[5:0];
  assign Op = Instruction[31:26];
  assign rd = Instruction[15:11];
  assign rs = Instruction[25:21];
  assign rt = Instruction[20:16];
  assign shamt = Instruction[10:6];
endmodule

module ALUControl (
  input  [1:0] ALUOp,
  input  [5:0] funct,
  output [2:0] ALUCtrl,
  output jumpregister
);

  wire ALUOp0PRIMA, ALUOp1PRIMA, and_1_out, and_2_out, and_3_out, and_4_out, and_5_out, and_6_out, and_7_out,
       and_8_out, and_9_out, and_10_out, and_11_out, and_12_out, and_13_out, and_14_out, and_15_out,
       and_16_out, and_17_out, and_18_out, and_19_out, and_20_out, and_21_out, and_23_out, and_25_out,
       and_26_out, and_27_out, and_28_out, F0PRIMA, F1PRIMA, F2PRIMA, F3PRIMA, F4PRIMA, F5PRIMA, or_1_out,
       or_2_out, or_3_out;

  not not_1 (ALUOp0PRIMA, ALUOp[0]);
  not not_2 (F5PRIMA, funct[5]);
  not not_3 (F4PRIMA, funct[4]);
  not not_4 (F3PRIMA, funct[3]);
  not not_5 (F2PRIMA, funct[2]);
  not not_6 (F1PRIMA, funct[1]);
  not not_7 (F0PRIMA, funct[0]);
  not not_8 (ALUOp1PRIMA, ALUOp[1]);
  and and_1 (and_1_out, funct[5], funct[2]);
  and and_2 (and_2_out, F4PRIMA, F3PRIMA);
  and and_3 (and_3_out, ALUOp[1], ALUOp0PRIMA);
  and and_4 (and_4_out, funct[5], funct[3]);
  and and_5 (and_5_out, funct[1], funct[0]);
  and and_6 (and_6_out, F4PRIMA, funct[1]);
  and and_7 (and_7_out, ALUOp[1], ALUOp0PRIMA);
  and and_8 (and_8_out, funct[5], F3PRIMA);
  and and_9 (and_9_out, funct[2], funct[0]);
  and and_10 (and_10_out, F2PRIMA, F0PRIMA);
  and and_11 (and_11_out, F5PRIMA, F3PRIMA);
  and and_12 (and_12_out, and_1_out, and_2_out, and_3_out);
  or or_1 (or_1_out, F1PRIMA, and_5_out);
  and and_13 (and_13_out, and_6_out, and_7_out);
  and and_14 (and_14_out, and_8_out, and_9_out);
  and and_15 (and_15_out, and_4_out, and_10_out);
  and and_16 (and_16_out, and_10_out, and_11_out);
  and and_17 (and_17_out, F4PRIMA, F3PRIMA);
  and and_18 (and_18_out, ALUOp[1], ALUOp0PRIMA);
  and and_19 (and_19_out, ALUOp1PRIMA, ALUOp[0]);
  and and_20 (and_20_out, F2PRIMA, funct[1]);
  and and_21 (and_21_out, funct[5], funct[2], F1PRIMA);
  and and_22 (ALUCtrl[0], and_12_out, or_1_out);
  and and_23 (and_23_out, and_17_out, and_18_out);
  or or_2 (or_2_out, and_14_out, and_15_out, and_16_out);
  or or_3 (or_3_out, and_20_out, and_21_out);
  and and_24 (ALUCtrl[1], and_13_out, or_2_out);
  and and_25 (and_25_out, and_23_out, F0PRIMA);
  and and_26 (and_26_out, and_25_out, or_3_out);
  or or_4 (ALUCtrl[2], and_19_out, and_26_out);
  and and_27 (and_27_out, ALUOp[1], ALUOp0PRIMA);
  and and_28 (and_28_out, F5PRIMA, F4PRIMA, funct[3], F2PRIMA, F1PRIMA, F0PRIMA);
  and and_29 (jumpregister, and_28_out, and_27_out);

  // Other names for the same wires on the sheet: F0 = funct[0]; F1 = funct[1]; F2 = funct[2]; F3 = funct[3];
  //   F4 = funct[4]; F5 = funct[5]
endmodule

module Control (
  input  [5:0] opcode,
  output RegDst,
  output Jump,
  output Branch,
  output MemRead,
  output MemtoReg,
  output [1:0] ALUOp,
  output MemWrite,
  output ALUSrc,
  output RegWrite,
  output SyngleByte,
  output JumpLink
);

  wire and_1_out, and_3_out, and_4_out, and_5_out, and_6_out, and_7_out, and_8_out, and_9_out, and_10_out,
       and_11_out, and_12_out, and_14_out, and_15_out, op0PRIMA, Op1Op0, op1PRIMA, Op1PRIMAOp0PRIMA,
       op2PRIMA, op3PRIMA, Op3PRIMAOp2PRIMA, op4PRIMA, op5PRIMA, Op5PRIMAOp4PRIMA, or_1_out, or_2_out,
       or_3_out, or_4_out, or_5_out;

  not not_1 (op5PRIMA, opcode[5]);
  not not_2 (op4PRIMA, opcode[4]);
  not not_3 (op3PRIMA, opcode[3]);
  not not_4 (op2PRIMA, opcode[2]);
  not not_5 (op1PRIMA, opcode[1]);
  not not_6 (op0PRIMA, opcode[0]);
  and and_1 (and_1_out, op3PRIMA, Op1PRIMAOp0PRIMA);
  or or_1 (or_1_out, and_1_out, Op1Op0);
  and and_2 (Op1Op0, opcode[1], opcode[0]);
  and and_3 (and_3_out, opcode[5], op4PRIMA, op2PRIMA);
  and and_4 (and_4_out, op1PRIMA, op0PRIMA);
  and and_5 (and_5_out, op5PRIMA, op4PRIMA, op3PRIMA);
  and and_6 (and_6_out, opcode[2], op1PRIMA, op0PRIMA);
  and and_7 (and_7_out, op2PRIMA, opcode[1]);
  and and_8 (and_8_out, op4PRIMA, op3PRIMA, op2PRIMA);
  or or_2 (or_2_out, Op1PRIMAOp0PRIMA, Op1Op0);
  and and_9 (and_9_out, opcode[5], op4PRIMA);
  and and_10 (and_10_out, Op3PRIMAOp2PRIMA, Op1PRIMAOp0PRIMA);
  and and_11 (and_11_out, Op5PRIMAOp4PRIMA, Op3PRIMAOp2PRIMA);
  and and_12 (and_12_out, opcode[5], op4PRIMA, Op3PRIMAOp2PRIMA);
  and and_13 (ALUSrc, and_3_out, or_1_out);
  and and_14 (and_14_out, and_3_out, Op1Op0);
  and and_15 (and_15_out, op5PRIMA, op4PRIMA, op3PRIMA, op2PRIMA);
  or or_3 (or_3_out, and_4_out, opcode[1]);
  and and_16 (JumpLink, and_11_out, Op1Op0);
  and and_17 (Op5PRIMAOp4PRIMA, op5PRIMA, op4PRIMA);
  and and_18 (Op3PRIMAOp2PRIMA, op3PRIMA, op2PRIMA);
  and and_19 (Op1PRIMAOp0PRIMA, op1PRIMA, op0PRIMA);
  and and_20 (Jump, Op5PRIMAOp4PRIMA, Op3PRIMAOp2PRIMA, opcode[1]);
  and and_21 (Branch, Op5PRIMAOp4PRIMA, op3PRIMA, opcode[2], Op1PRIMAOp0PRIMA);
  or or_4 (or_4_out, and_6_out, and_7_out);
  and and_22 (SyngleByte, and_9_out, and_10_out);
  and and_23 (MemRead, and_12_out, or_5_out);
  or or_5 (or_5_out, Op1Op0, Op1PRIMAOp0PRIMA);
  and and_24 (MemWrite, and_14_out, opcode[3]);
  and and_25 (ALUOp[1], and_15_out, or_3_out);
  and and_26 (ALUOp[0], and_5_out, or_4_out);
  and and_27 (RegWrite, and_8_out, or_2_out);
  and and_28 (RegDst, Op5PRIMAOp4PRIMA, Op3PRIMAOp2PRIMA, Op1PRIMAOp0PRIMA);

  assign MemtoReg = ALUSrc;

  // Other names for the same wires on the sheet: op0 = opcode[0]; op1 = opcode[1]; op2 = opcode[2]; op3 = opcode[3];
  //   op4 = opcode[4]; op5 = opcode[5]
endmodule

module MemoryData (
  input  [31:0] address,
  input  [31:0] WriteData,
  input  MemWrite,
  input  MemRead,
  input  CLK,
  input  Reset,
  output [31:0] ReadData,
  output [7:0] MemoryByte
);

  // Probe on address[25:2]
  RAM #(.addrWidth(24), .asyncread("true"), .clearpin("true"), .dataWidth(32), .\type ("nonvolatile")) ram_1 (
    .addr(address[25:2]), .we(MemWrite), .oe(MemRead), .clk(CLK), .din(WriteData), .dout(ReadData),
    .clr(Reset));
  // Probe on ReadData
  // Probe on address[1:0]
  BitSelector #(.group(8), .width(32)) bitselector_1 (.in(ReadData), .out(MemoryByte), .sel(address[1:0]));

  // Other names for the same wires on the sheet: BitsDeSeleccion[1:0] = address[1:0]
endmodule

module ejemplo (
  input  [1:0] ALUOp,
  input  [5:0] funct,
  output [2:0] ALUCtrl
);

  wire ALUOp0PRIMA, ALUOp1PRIMA, and_1_out, and_2_out, and_3_out, and_4_out, and_5_out, and_6_out, F0PRIMA,
       F1PRIMA, F2PRIMA, F3PRIMA, F4PRIMA, F5PRIMA, or_1_out;

  not not_1 (ALUOp0PRIMA, ALUOp[0]);
  not not_2 (F5PRIMA, funct[5]);
  not not_3 (F4PRIMA, funct[4]);
  not not_4 (F3PRIMA, funct[3]);
  not not_5 (F2PRIMA, funct[2]);
  not not_6 (F1PRIMA, funct[1]);
  not not_7 (F0PRIMA, funct[0]);
  not not_8 (ALUOp1PRIMA, ALUOp[1]);
  and and_1 (and_1_out, funct[5], F2PRIMA, funct[1]);
  and and_2 (and_2_out, funct[5], funct[2], F1PRIMA);
  and and_3 (and_3_out, F5PRIMA, F2PRIMA, funct[1]);
  and and_4 (and_4_out, ALUOp[1], ALUOp0PRIMA, F4PRIMA, F3PRIMA, F0PRIMA);
  or or_1 (or_1_out, and_1_out, and_2_out, and_3_out);
  and and_5 (and_5_out, and_4_out, or_1_out);
  and and_6 (and_6_out, ALUOp1PRIMA, ALUOp[0]);
  or or_2 (ALUCtrl[2], and_5_out, and_6_out);

  // Other names for the same wires on the sheet: F0 = funct[0]; F1 = funct[1]; F2 = funct[2]; F3 = funct[3];
  //   F4 = funct[4]; F5 = funct[5]
endmodule
